// Logisim project ALU.circ as structural Verilog: 1 circuit, main circuit ALU
module ALU (
  input  [31:0] A,
  input  [31:0] B,
  input  [4:0] Shift,
  input  [3:0] Codop,
  input  CarryIn,
  output [31:0] S,
  output [3:0] Flags
);

  wire CarryOut_ADC, CarryOut_ASR, CarryOut_CMN, CarryOut_CMP, CarryOut_LSL, CarryOut_RSB, CarryOut_SBC,
       comparator_1_eq, comparator_1_gt, comparator_1_lt, comparator_3_eq, comparator_4_eq, comparator_5_eq,
       not_4_out, or_2_out, Overflow_ADC, Overflow_CMN, Overflow_CMP, Overflow_SBC, subtractor_1_bout,
       subtractor_3_bout, xnor_1_out, xnor_2_out, xor_2_out, xor_3_out, xor_4_out, xor_5_out, xor_6_out,
       xor_7_out;
  wire [4:0] negator_1_out, negator_2_out, subtractor_4_out;
  wire [31:0] multiplexer_1_out, not_1_out, sortie_ADC, sortie_AND, sortie_ASR, sortie_BIC, sortie_CMN,
       sortie_CMP, sortie_EOR, sortie_LSL, sortie_LSR, sortie_MUL, sortie_MVN, sortie_ORR, sortie_ROR,
       sortie_RSB, sortie_SBC, sortie_TST;

  Subtractor #(.width(32)) subtractor_1 (.a(B), .b(A), .out(sortie_CMP), .bout(subtractor_1_bout));  // open: bin
  Multiplier #(.width(32)) multiplier_1 (.a(A), .b(B), .out(sortie_MUL));  // open: cin, cout
  assign not_1_out = ~A;  // NOT_Gate not_1, 32 bits wide
  assign sortie_MVN = ~A;  // NOT_Gate not_2, 32 bits wide
  assign sortie_AND = A & B;  // AND_Gate and_1, 32 bits wide
  assign sortie_EOR = A ^ B;  // XOR_Gate xor_1, 32 bits wide
  Shifter #(.width(32)) shifter_1 (.in(B), .\dist (Shift), .out(sortie_LSL));
  Shifter #(.shift("lr"), .width(32)) shifter_2 (.in(B), .\dist (Shift), .out(sortie_LSR));
  Shifter #(.shift("ar"), .width(32)) shifter_3 (.in(B), .\dist (Shift), .out(sortie_ASR));
  Adder #(.width(32)) adder_1 (.a(A), .b(B), .out(sortie_ADC), .cin(CarryIn), .cout(CarryOut_ADC));
  Shifter #(.shift("rr"), .width(32)) shifter_4 (.in(B), .\dist (Shift), .out(sortie_ROR));
  assign sortie_TST = A & B;  // AND_Gate and_2, 32 bits wide
  Subtractor #(.width(32)) subtractor_2 (.a({32{1'b0}}), .b(A), .out(sortie_RSB));  // open: bin, bout
  not not_3 (CarryOut_CMP, subtractor_1_bout);
  Adder #(.width(32)) adder_2 (.a(A), .b(B), .out(sortie_CMN), .cout(CarryOut_CMN));  // open: cin
  assign sortie_ORR = A | B;  // OR_Gate or_1, 32 bits wide
  assign sortie_BIC = B & not_1_out;  // AND_Gate and_3, 32 bits wide
  not not_4 (not_4_out, CarryIn);
  Subtractor #(.width(32)) subtractor_3 (.a(B), .b(A), .out(sortie_SBC), .bin(not_4_out), .bout(subtractor_3_bout));
  not not_5 (CarryOut_SBC, subtractor_3_bout);
  Comparator #(.width(32)) comparator_1 (
    .a({32{1'b0}}), .b(A), .gt(comparator_1_gt), .eq(comparator_1_eq), .lt(comparator_1_lt));
  BitSelector #(.width(32)) bitselector_1 (.in(B), .out(CarryOut_ASR), .sel(subtractor_4_out));
  Subtractor #(.width(5)) subtractor_4 (.a(Shift), .b(5'b00001), .out(subtractor_4_out));  // open: bin, bout
  BitSelector #(.width(32)) bitselector_2 (.in(B), .out(CarryOut_LSL), .sel(negator_1_out));
  Negator #(.width(5)) negator_1 (.in(Shift), .out(negator_1_out));
  nor nor_1 (CarryOut_RSB, comparator_1_gt, comparator_1_lt);
  Negator #(.width(5)) negator_2 (.in(Shift), .out(negator_2_out));
  Multiplexer #(.select(4), .width(32)) multiplexer_1 (
    .in0(sortie_AND), .in1(sortie_EOR), .in2(sortie_LSL), .in3(sortie_LSR), .in4(sortie_ASR),
    .in5(sortie_ADC), .in6(sortie_SBC), .in7(sortie_ROR), .in8(sortie_TST), .in9(sortie_RSB),
    .in10(sortie_CMP), .in11(sortie_CMN), .in12(sortie_ORR), .in13(sortie_MUL), .in14(sortie_BIC),
    .in15(sortie_MVN), .out(multiplexer_1_out), .sel(Codop));
  Multiplexer #(.select(4)) multiplexer_2 (
    .in0(1'b0), .in1(1'b0), .in2(CarryOut_LSL), .in3(CarryOut_ASR), .in4(CarryOut_ASR), .in5(CarryOut_ADC),
    .in6(CarryOut_SBC), .in7(sortie_ROR[31]), .in8(1'b0), .in9(1'b0), .in10(CarryOut_CMP),
    .in11(CarryOut_CMN), .in12(1'b0), .in13(1'b0), .in14(1'b0), .in15(1'b0), .out(Flags[1]), .sel(Codop));
  BitSelector #(.width(32)) bitselector_3 (.in(multiplexer_1_out), .out(Flags[3]), .sel({5{1'b1}}));
  xor xor_2 (xor_2_out, B[31], sortie_ADC[31]);
  xnor xnor_1 (xnor_1_out, A[31], B[31]);
  xor xor_3 (xor_3_out, B[31], sortie_SBC[31]);
  xor xor_4 (xor_4_out, A[31], B[31]);
  xor xor_5 (xor_5_out, B[31], sortie_CMP[31]);
  xor xor_6 (xor_6_out, A[31], B[31]);
  xor xor_7 (xor_7_out, B[31], sortie_CMN[31]);
  xnor xnor_2 (xnor_2_out, A[31], B[31]);
  Comparator #(.width(32)) comparator_2 (.a(multiplexer_1_out), .b({32{1'b0}}), .eq(Flags[2]));  // open: gt, lt
  Multiplexer #(.select(4)) multiplexer_3 (
    .in0(1'b0), .in1(1'b0), .in2(1'b0), .in3(1'b0), .in4(1'b0), .in5(Overflow_ADC), .in6(Overflow_SBC),
    .in7(1'b0), .in8(1'b0), .in9(1'b0), .in10(Overflow_CMP), .in11(Overflow_CMN), .in12(1'b0), .in13(1'b0),
    .in14(1'b0), .in15(1'b0), .out(Flags[0]), .sel(Codop));
  and and_4 (Overflow_ADC, xor_2_out, xnor_1_out);
  and and_5 (Overflow_SBC, xor_3_out, xor_4_out);
  and and_6 (Overflow_CMP, xor_5_out, xor_6_out);
  and and_7 (Overflow_CMN, xor_7_out, xnor_2_out);
  Comparator #(.width(4)) comparator_3 (.a(Codop), .b(4'b1010), .eq(comparator_3_eq));  // open: gt, lt
  Comparator #(.width(4)) comparator_4 (.a(Codop), .b(4'b1011), .eq(comparator_4_eq));  // open: gt, lt
  Comparator #(.width(4)) comparator_5 (.a(Codop), .b(4'b1000), .eq(comparator_5_eq));  // open: gt, lt
  Multiplexer #(.width(32)) multiplexer_4 (.in0(multiplexer_1_out), .in1(B), .out(S), .sel(or_2_out));
  or or_2 (or_2_out, comparator_3_eq, comparator_4_eq, comparator_5_eq);
  // also tied to GND on the sheet: comparator_1_eq

  // Other names for the same wires on the sheet: CarryOut_LSR = CarryOut_ASR; Cin = CarryIn; V = Flags[0];
  //   C = Flags[1]; Z = Flags[2]; N = Flags[3]

  // Notes on the sheet:
  //   Note: for ROR, C = N
  //   Note 2: assume that shift > 0 for LSL and LSR
endmodule
