// Logisim project Ctl_Conditional.circ as structural Verilog: 1 circuit, main circuit Conditional
module Conditional (
  input  Enable,
  input  [15:0] Instruction,
  input  Z,
  input  C,
  input  N,
  input  V,
  output [10:0] Offset,
  output Verified
);

  wire CC, comparator_2_eq, GE, GT, HI, LE, LS, LT, multiplexer_2_out, multiplexer_3_out, NE, not_6_out, PL,
       VC;
  wire [10:0] bit_extender_1_out, multiplexer_1_out;

  not not_1 (NE, Z);
  not not_2 (CC, C);
  not not_3 (PL, N);
  not not_4 (VC, V);
  and and_1 (HI, C, NE);
  or or_1 (LS, CC, Z);
  Comparator #(.width(1)) comparator_1 (.a(N), .b(V), .eq(GE));  // open: gt, lt
  Comparator #(.width(1)) comparator_2 (.a(N), .b(V), .eq(comparator_2_eq));  // open: gt, lt
  and and_2 (GT, NE, GE);
  or or_2 (LE, Z, LT);
  not not_5 (LT, comparator_2_eq);
  assign bit_extender_1_out = {{3{Instruction[7]}}, Instruction[7:0]};  // Bit_Extender bit_extender_1
  Multiplexer #(.width(11)) multiplexer_1 (
    .in0(bit_extender_1_out), .in1(Instruction[10:0]), .out(multiplexer_1_out), .sel(Instruction[13]));
  Multiplexer #(.select(4)) multiplexer_2 (
    .in0(Z), .in1(NE), .in2(C), .in3(CC), .in4(N), .in5(PL), .in6(V), .in7(VC), .in8(HI), .in9(LS),
    .in10(GE), .in11(LT), .in12(GT), .in13(LE), .in14(1'b1), .out(multiplexer_2_out), .sel(Instruction[11:8]));  // open: in15
  assign Offset = Verified ? multiplexer_1_out : 11'bz;  // Controlled_Buffer controlled_buffer_1
  not not_6 (not_6_out, Instruction[12]);
  Pull_Resistor pull_resistor_1 (.node(Offset));
  Multiplexer multiplexer_3 (.in0(multiplexer_2_out), .in1(1'b1), .out(multiplexer_3_out), .sel(not_6_out));
  Multiplexer multiplexer_4 (.in0(1'b0), .in1(multiplexer_3_out), .out(Verified), .sel(Enable));

  // Other names for the same wires on the sheet: CS = C; EQ = Z; Imm8[7:0] = Instruction[7:0];
  //   Imm11[10:0] = Instruction[10:0]; COND[3:0] = Instruction[11:8]; BIT12 = Instruction[12];
  //   BIT13 = Instruction[13]; MI = N; VS = V
endmodule
