// Logisim project Ctl_Data_Processing.circ as structural Verilog: 1 circuit, main circuit Data_Processing
module Data_Processing (
  input  Enable,
  input  [15:0] Instruction,
  output [2:0] Rd,
  output [2:0] Rn,
  output [2:0] Rm,
  output [3:0] ALU_Opcode,
  output [3:0] Flags_Update_Mask
);

  wire C, comparator_1_eq, comparator_2_eq, or_1_out;
  wire [0:0] Flags_Update_Mask_t;
  wire [2:0] Rm_t, Rn_t;

  Multiplexer #(.select(4)) multiplexer_1 (
    .in0(1'b0), .in1(1'b0), .in2(1'b0), .in3(1'b0), .in4(1'b0), .in5(1'b1), .in6(1'b1), .in7(1'b0),
    .in8(1'b0), .in9(1'b1), .in10(1'b1), .in11(1'b1), .in12(1'b0), .in13(1'b0), .in14(1'b0), .in15(1'b0),
    .out(Flags_Update_Mask_t[0]), .sel(Instruction[9:6]));
  Comparator #(.width(4)) comparator_1 (.a(Instruction[9:6]), .b(4'b1001), .eq(comparator_1_eq));  // open: gt, lt
  Comparator #(.width(4)) comparator_2 (.a(Instruction[9:6]), .b(4'b1101), .eq(comparator_2_eq));  // open: gt, lt
  Multiplexer #(.width(3)) multiplexer_2 (.in0(Instruction[5:3]), .in1(Instruction[2:0]), .out(Rm_t), .sel(or_1_out));
  Multiplexer #(.width(3)) multiplexer_3 (.in0(Instruction[2:0]), .in1(Instruction[5:3]), .out(Rn_t), .sel(or_1_out));
  or or_1 (or_1_out, comparator_1_eq, comparator_2_eq);
  nand nand_1 (C, or_1_out, Instruction[8]);
  Multiplexer #(.width(3)) multiplexer_4 (.in0(3'b000), .in1(Instruction[2:0]), .out(Rd), .sel(Enable));
  Multiplexer #(.width(3)) multiplexer_5 (.in0(3'b000), .in1(Rn_t), .out(Rn), .sel(Enable));
  Multiplexer #(.width(3)) multiplexer_6 (.in0(3'b000), .in1(Rm_t), .out(Rm), .sel(Enable));
  Multiplexer #(.width(4)) multiplexer_7 (.in0(4'b0000), .in1(Instruction[9:6]), .out(ALU_Opcode), .sel(Enable));
  Multiplexer #(.width(4)) multiplexer_8 (
    .in0(4'b0000), .in1({2'b11, C, Flags_Update_Mask_t[0]}), .out(Flags_Update_Mask), .sel(Enable));

  // Other names for the same wires on the sheet: V = Flags_Update_Mask_t[0]; Flags_Update_Mask_t[1] = C;
  //   Rd_t[2:0] = Instruction[2:0]; ALU_Opcode_t[3:0] = Instruction[9:6]

  // Notes on the sheet:
  //   Note 2: RSB instruction has Rn as 1st operand.
  //   MUL instruction has Rn as 1st operand and Rdm as 2nd operand
  //   For simplification purposes, Rm is used for 1st operand both here and in the ALU.
  //   Note: instructions that does not save the result will still have the second operand as the destination register, the ALU will copy the second register to the destination register
  //   Pull output low on Enable = 0
endmodule
