// Logisim project Ctl_Flags_APSR.circ as structural Verilog: 1 circuit, main circuit Flags_APSR
module Flags_APSR (
  input  [3:0] Update_Mask,
  input  [3:0] Flags_In,
  input  Clk,
  input  Rst,
  output [3:0] Flags_Out
);

  Register #(.width(1)) register_1 (.D(Flags_In[0]), .en(Update_Mask[0]), .clk(Clk), .Q(Flags_Out[0]), .clr(Rst));
  Register #(.width(1)) register_2 (.D(Flags_In[1]), .en(Update_Mask[1]), .clk(Clk), .Q(Flags_Out[1]), .clr(Rst));
  Register #(.width(1)) register_3 (.D(Flags_In[2]), .en(Update_Mask[2]), .clk(Clk), .Q(Flags_Out[2]), .clr(Rst));
  Register #(.width(1)) register_4 (.D(Flags_In[3]), .en(Update_Mask[3]), .clk(Clk), .Q(Flags_Out[3]), .clr(Rst));

  // Other names for the same wires on the sheet: Clock = Clk; Flag_1 = Flags_In[0]; Flag_2 = Flags_In[1];
  //   Flag_3 = Flags_In[2]; Flag_4 = Flags_In[3]; N = Flags_Out[0]; Z = Flags_Out[1]; C = Flags_Out[2];
  //   V = Flags_Out[3]; Reset = Rst; Mask_1 = Update_Mask[0]; Mask_2 = Update_Mask[1]; Mask_3 = Update_Mask[2];
  //   Mask_4 = Update_Mask[3]
endmodule
