// Logisim project Ctl_Load_Store.circ as structural Verilog: 1 circuit, main circuit Load_Store
module Load_Store (
  input  [15:0] Instruction,
  input  Enable,
  input  Clk,
  input  Reset,
  input  [31:0] Stack_Pointer,
  output Store,
  output Load,
  output PC_Hold,
  output [2:0] Rmd,
  output [31:0] RAM_Addr
);

  wire and_1_out, d_ff_1_q, not_1_out, not_2_out;
  wire [31:0] adder_1_out, bit_extender_1_out;

  not not_1 (not_1_out, d_ff_1_q);
  not not_2 (not_2_out, Instruction[11]);
  D_Flip_Flop d_ff_1 (.D(and_1_out), .clk(Clk), .Q(d_ff_1_q), .reset(Reset));  // open: Qn, preset
  and and_1 (and_1_out, not_1_out, Load);
  and and_2 (Store, Enable, not_2_out);
  Multiplexer multiplexer_1 (.in0(1'b0), .in1(d_ff_1_q), .out(PC_Hold), .sel(Enable));
  and and_3 (Load, Enable, Instruction[11]);
  Multiplexer #(.width(3)) multiplexer_2 (.in0(3'b000), .in1(Instruction[10:8]), .out(Rmd), .sel(Enable));
  assign bit_extender_1_out = {{24{Instruction[7]}}, Instruction[7:0]};  // Bit_Extender bit_extender_1
  Adder #(.width(32)) adder_1 (.a(Stack_Pointer), .b(bit_extender_1_out), .out(adder_1_out));  // open: cin, cout
  Multiplexer #(.width(32)) multiplexer_3 (.in0({32{1'b0}}), .in1(adder_1_out), .out(RAM_Addr), .sel(Enable));

  // Other names for the same wires on the sheet: CKL = Clk; imm8[7:0] = Instruction[7:0];
  //   Rmd_t[2:0] = Instruction[10:8]; b11 = Instruction[11]

  // Notes on the sheet:
  //   Instruction: pull=down
  //   Delay load and hold PC for 1 cycle for the RAM to send out requested data 
endmodule
