// Logisim project Ctl_Shift_Add_Sub_Mov.circ as structural Verilog: 1 circuit, main circuit Shift_Add_Sub_Mov
module Shift_Add_Sub_Mov (
  input  Enable,
  input  [15:0] Instruction,
  output Carry,
  output [2:0] Rm,
  output [2:0] Rn,
  output [2:0] out_6,
  output [2:0] Rd,
  output [4:0] Imm5,
  output [3:0] Flags_Update_Mask,
  output [3:0] ALU_Opcode,
  output Imm32_Enable,
  output [31:0] Imm32
);

  wire ADD3, ADDS, ADDS8, and_1_out, and_2_out, and_14_out, and_15_out, and_16_out, ASRS, CMPS, LSLS, LSRS,
       MOVS, or_9_out, or_10_out, or_13_out, Rd2_enable, Rd_enable, Rdn_enable, Rn_enable, SUB3, SUBS, SUBS8;
  wire [1:0] bit_extender_2_out, bit_extender_4_out, bit_extender_5_out;
  wire [2:0] multiplexer_11_out, Rd2_bis, Rd_bis, Rdn_bis, Rm2_bis, Rn_bis;
  wire [3:0] ALU, Flags, pull_resistor_5_node, pull_resistor_6_node, pull_resistor_7_node,
       pull_resistor_8_node, pull_resistor_9_node, pull_resistor_10_node, pull_resistor_11_node,
       pull_resistor_12_node, pull_resistor_13_node, pull_resistor_14_node, pull_resistor_15_node;
  wire [3:3] NZC, NZCV;
  wire [31:0] bit_extender_1_out, bit_extender_3_out, multiplexer_9_out, multiplexer_10_out, negator_1_out;

  or or_1 (NZCV[3], SUBS8, SUBS, SUB3, CMPS, ADD3, ADDS, ADDS8);
  or or_2 (NZC[3], LSLS, ASRS, LSRS);
  and and_1 (and_1_out, Rd2_enable, Enable);
  assign Flags = {4{NZCV[3]}} | {{3{NZC[3]}}, 1'b0} | {{2{MOVS}}, 2'b00};  // OR_Gate or_3, 4 bits wide
  or or_4 (Rdn_enable, MOVS, CMPS, ADDS8, SUBS8);
  or or_5 (Rd2_enable, LSLS, ASRS, LSRS);
  or or_6 (Rd_enable, ADDS, SUBS, ADD3, SUB3);
  Multiplexer #(.width(3)) multiplexer_1 (.in0(3'b000), .in1(Instruction[2:0]), .out(Rd2_bis), .sel(and_1_out));
  or or_7 (Rn_enable, ADDS, SUBS, ADD3, SUB3);
  Multiplexer #(.width(3)) multiplexer_2 (.in0(3'b000), .in1(Instruction[10:8]), .out(Rdn_bis), .sel(and_2_out));
  and and_2 (and_2_out, Rdn_enable, Enable);
  and and_3 (ADDS, ~Instruction[9], ~Instruction[10], Instruction[11], Instruction[12], ~Instruction[13]);  // AND_Gate
  and and_4 (SUBS, Instruction[9], ~Instruction[10], Instruction[11], Instruction[12], ~Instruction[13]);  // AND_Gate
  and and_5 (ADD3, ~Instruction[9], Instruction[10], Instruction[11], Instruction[12], ~Instruction[13]);  // AND_Gate
  and and_6 (SUB3, Instruction[9], Instruction[10], Instruction[11], Instruction[12], ~Instruction[13]);  // AND_Gate
  and and_7 (LSLS, ~Instruction[11], ~Instruction[12], ~Instruction[13]);  // AND_Gate
  and and_8 (LSRS, Instruction[11], ~Instruction[12], ~Instruction[13]);  // AND_Gate
  and and_9 (ASRS, ~Instruction[11], Instruction[12], ~Instruction[13]);  // AND_Gate
  and and_10 (MOVS, ~Instruction[11], ~Instruction[12], Instruction[13]);  // AND_Gate
  and and_11 (CMPS, Instruction[11], ~Instruction[12], Instruction[13]);  // AND_Gate
  and and_12 (ADDS8, ~Instruction[11], Instruction[12], Instruction[13]);  // AND_Gate
  and and_13 (SUBS8, Instruction[11], Instruction[12], Instruction[13]);
  Multiplexer #(.width(3)) multiplexer_3 (.in0(3'b000), .in1(Instruction[2:0]), .out(Rd_bis), .sel(and_14_out));
  and and_14 (and_14_out, Rd_enable, Enable);
  and and_15 (and_15_out, Rn_enable, Enable);
  assign ALU = pull_resistor_5_node | pull_resistor_6_node | pull_resistor_7_node | pull_resistor_8_node | pull_resistor_9_node | pull_resistor_10_node | pull_resistor_11_node | pull_resistor_12_node | pull_resistor_13_node | pull_resistor_14_node | pull_resistor_15_node;  // OR_Gate or_8, 4 bits wide
  Multiplexer #(.width(3)) multiplexer_4 (.in0(3'b000), .in1(Instruction[5:3]), .out(Rn_bis), .sel(and_15_out));
  and and_16 (and_16_out, Rd2_enable, Enable);
  assign bit_extender_1_out = {{24{1'b0}}, Instruction[7:0]};  // Bit_Extender bit_extender_1
  Multiplexer #(.width(3)) multiplexer_5 (.in0(3'b000), .in1(Instruction[5:3]), .out(Rm2_bis), .sel(and_16_out));
  assign Imm32_Enable = Enable ? or_9_out : 1'bz;  // Controlled_Buffer controlled_buffer_1
  Pull_Resistor pull_resistor_1 (.node(Imm32_Enable));
  Negator #(.width(32)) negator_1 (.in(bit_extender_1_out), .out(negator_1_out));
  assign ALU_Opcode = Enable ? ALU : 4'bz;  // Controlled_Buffer controlled_buffer_2
  Pull_Resistor pull_resistor_2 (.node(ALU_Opcode));
  or or_9 (or_9_out, MOVS, CMPS, ADDS8, SUBS8, or_13_out);
  Pull_Resistor pull_resistor_3 (.node(Carry));
  or or_10 (or_10_out, SUBS8, SUBS, SUB3);
  assign Carry = Enable ? or_10_out : 1'bz;  // Controlled_Buffer controlled_buffer_3
  Multiplexer #(.select(2), .width(3)) multiplexer_6 (
    .in0(3'b000), .in1(Instruction[8:6]), .in2(Instruction[5:3]), .in3(Instruction[8:6]), .out(Rm),
    .sel(bit_extender_2_out));
  assign bit_extender_2_out = {{1{1'b0}}, Enable};  // Bit_Extender bit_extender_2
  assign Rn = Rdn_bis | Rn_bis | Rm2_bis;  // OR_Gate or_11, 3 bits wide
  assign Rd = Rdn_bis | Rd2_bis | Rd_bis;  // OR_Gate or_12, 3 bits wide
  Multiplexer #(.width(5)) multiplexer_7 (.in0({5{1'b0}}), .in1(Instruction[10:6]), .out(Imm5), .sel(Enable));
  Multiplexer #(.width(4)) multiplexer_8 (.in0(4'b0000), .in1(Flags), .out(Flags_Update_Mask), .sel(Enable));
  assign bit_extender_3_out = {{29{1'b0}}, Instruction[8:6]};  // Bit_Extender bit_extender_3
  Multiplexer #(.width(32)) multiplexer_9 (
    .in0(bit_extender_1_out), .in1(negator_1_out), .out(multiplexer_9_out), .sel(MOVS));
  or or_13 (or_13_out, ADD3, SUB3);
  assign Imm32 = Enable ? multiplexer_10_out : 32'bz;  // Controlled_Buffer controlled_buffer_4
  Multiplexer #(.width(32)) multiplexer_10 (
    .in0(bit_extender_3_out), .in1(multiplexer_9_out), .out(multiplexer_10_out), .sel(Instruction[13]));
  Pull_Resistor pull_resistor_4 (.node(Imm32));
  Pull_Resistor pull_resistor_5 (.node(pull_resistor_5_node));
  assign pull_resistor_5_node = ADDS ? 4'b0101 : 4'bz;  // Controlled_Buffer controlled_buffer_5
  Pull_Resistor pull_resistor_6 (.node(pull_resistor_6_node));
  assign pull_resistor_6_node = SUBS ? 4'b0110 : 4'bz;  // Controlled_Buffer controlled_buffer_6
  Pull_Resistor pull_resistor_7 (.node(pull_resistor_7_node));
  assign pull_resistor_7_node = ADD3 ? 4'b0101 : 4'bz;  // Controlled_Buffer controlled_buffer_7
  Pull_Resistor pull_resistor_8 (.node(pull_resistor_8_node));
  assign pull_resistor_8_node = SUB3 ? 4'b0110 : 4'bz;  // Controlled_Buffer controlled_buffer_8
  Pull_Resistor pull_resistor_9 (.node(pull_resistor_9_node));
  assign pull_resistor_9_node = LSRS ? 4'b0011 : 4'bz;  // Controlled_Buffer controlled_buffer_9
  Pull_Resistor pull_resistor_10 (.node(pull_resistor_10_node));
  assign pull_resistor_10_node = LSLS ? 4'b0010 : 4'bz;  // Controlled_Buffer controlled_buffer_10
  Pull_Resistor pull_resistor_11 (.node(pull_resistor_11_node));
  assign pull_resistor_11_node = ASRS ? 4'b0100 : 4'bz;  // Controlled_Buffer controlled_buffer_11
  Pull_Resistor pull_resistor_12 (.node(pull_resistor_12_node));
  assign pull_resistor_12_node = CMPS ? 4'b1010 : 4'bz;  // Controlled_Buffer controlled_buffer_12
  Pull_Resistor pull_resistor_13 (.node(pull_resistor_13_node));
  assign pull_resistor_13_node = ADDS8 ? 4'b0101 : 4'bz;  // Controlled_Buffer controlled_buffer_13
  Pull_Resistor pull_resistor_14 (.node(pull_resistor_14_node));
  assign pull_resistor_14_node = MOVS ? 4'b1001 : 4'bz;  // Controlled_Buffer controlled_buffer_14
  Pull_Resistor pull_resistor_15 (.node(pull_resistor_15_node));
  assign pull_resistor_15_node = SUBS8 ? 4'b0110 : 4'bz;  // Controlled_Buffer controlled_buffer_15
  assign bit_extender_4_out = {{1{1'b0}}, Enable};  // Bit_Extender bit_extender_4
  assign bit_extender_5_out = {{1{1'b0}}, Enable};  // Bit_Extender bit_extender_5
  Multiplexer #(.select(2), .width(3)) multiplexer_11 (
    .in0(3'b000), .in1(Instruction[5:3]), .in2(Instruction[10:8]), .in3(Instruction[10:8]),
    .out(multiplexer_11_out), .sel(bit_extender_4_out));
  Multiplexer #(.select(2), .width(3)) multiplexer_12 (
    .in0(3'b000), .in1(Instruction[2:0]), .in2(Instruction[2:0]), .in3(Instruction[10:8]),
    .sel(bit_extender_5_out));  // open: out

  // Other names for the same wires on the sheet: imm8[7:0] = Instruction[7:0]; Rd2[2:0] = Instruction[2:0];
  //   Rd_t[2:0] = Instruction[2:0]; Rm2[2:0] = Instruction[5:3]; Rn_t[2:0] = Instruction[5:3];
  //   imm3[2:0] = Instruction[8:6]; imm5_t[4:0] = Instruction[10:6]; Rm_t[2:0] = Instruction[8:6];
  //   Rdn[2:0] = Instruction[10:8]; opcode[4:0] = Instruction[13:9]; opcode2[2:0] = Instruction[13:11];
  //   opcode3[2:0] = Instruction[13:11]; b13 = Instruction[13]; NZ[3:2] = {2{MOVS}}; NZC[2:1] = {2{NZC[3]}};
  //   NZCV[2:0] = {3{NZCV[3]}}

  // Notes on the sheet:
  //   when imm3, imm32 is enabled
  //   Note 3: Imm32_Enable forces the use of the immediate for Rm register
  //   Note: ALU uses Rn register for shifts. Use Rn instead of Rm for shifts (immediate) here too
  //   Pull output low on Enable = 0
  //   Note 2: MOV uses RSB ALU opcode with Imm8 reversed so that it is copied to output register
  //   ALU will use Imm32 instead of Rm
  //   only ADD and SUB use Rm
  //   Enable carry for SUB since it is reversed in ALU
endmodule
